# Fritzing sketch Voltage_LED (saved by Fritzing 0.9.10b)
breadboards: 1

parts:
  Part1 = INA219 High Side DC Current Sensor Breakout [part_number=904]
  Part2 = Arduino Mega 2560 (Rev3)
  Part3 = INA219 High Side DC Current Sensor Breakout [part_number=904]
  LED1 = smd LED [color="Red (633nm)" package="0805 [SMD]"]  # not connected
  LED2 = smd LED [color="Green (555nm)" package="1206 [SMD]"]
  R1 = Resistor [tolerance=±5% resistance=220 package="1206 [SMD]"]
  R2 = Resistor [tolerance=±5% resistance=220 package="1206 [SMD]"]
  LED3 = smd LED [color="Green (555nm)" package="1206 [SMD]"]  # not connected
  LED4 = smd LED [color="Red (633nm)" package="1206 [SMD]"]
  R3 = Resistor [tolerance=±5% resistance=220 package="0603 [SMD]"]
  R4 = Resistor [tolerance=±5% resistance=220 package="1206 [SMD]"]
  R5 = Rotary Potentiometer (Large) [maximum_resistance=10kΩ knob_status=50% power=0.5W package=THT]
  R6 = Rotary Potentiometer (Large) [maximum_resistance=10kΩ knob_status=50% power=0.5W package=THT]

nets:
  VCC: Part1.VCC, Part2.5V, Part3.VCC, R5.leg2
  GND: Part1.GND, Part2.GND, Part3.GND, LED2.cathode, LED4.cathode, R5.leg1, R6.leg1
  N1: Part1.SCL, Part2.D21/SCL, Part3.SCL
  N2: Part1.SDA, Part2.D20/SDA, Part3.SDA
  N3: Part2.A0, R5.wiper
  N4: Part2.A1, R6.wiper
  N5: Part2.D8_PWM, R3.Pin_1
  N6: Part2.D5_PWM, R2.Pin_0
  N7: Part2.D6_PWM, R1.Pin_1
  N8: Part2.D7_PWM, R4.Pin_0
  N9: LED2.anode, R2.Pin_1
  N10: LED4.anode, R3.Pin_0

custom parts:
  INA219 High Side DC Current Sensor Breakout: This breakout board will solve all your power-monitoring problems. Instead of struggling with two multimeters, you can just use the handy INA219B chip on this breakout to both measure both the high side voltage and DC current draw over I2C with 1% precision. Most current-measuring devices such as our current panel meter are only good for low side measuring. That means that unless you want to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

// code stored in the sketch: Fritzibg_test.ino
// Use TcBUTTON library
#include <TcPINOUT.h>



/*----------------- SET PINOUT 1-----------------*/
#define PIN_LED_GREEN_1 5
#define PIN_LED_RED_1 6


TcPINOUT LED_GREEN_1(PIN_LED_GREEN_1);
TcPINOUT LED_RED_1(PIN_LED_RED_1);
/*----------------- SET PINOUT 1-----------------*/
#define PIN_LED_GREEN_2 7
#define PIN_LED_RED_2 8


TcPINOUT LED_GREEN_2(PIN_LED_GREEN_2);
TcPINOUT LED_RED_2(PIN_LED_RED_2);


/*----------------- VARIABLES -----------------*/


const float current_limit = 80;
const float voltage_limit = 2.5;


void setup() {
  Serial.begin(9600);
}


void loop() {


  /*------------- GET VALUE 1 -----------------*/
 float current_sensor_1 = 100;  // Read current from  sensor 1
 float voltage_1 = 2.3;        // Read voltage from  sensor 1
// Call function validateVoltage
 validateVoltage(current_sensor_1 ,voltage_1,LED_GREEN_1, LED_RED_1);



 /*-------------- GET VALUE 2 -----------------*/
 float current_sensor_2 = 100;  // Read current from  sensor 2
 float voltage_2 = 2.3;        // Read voltage from  sensor 2
 // Call function validateVoltage
 validateVoltage(current_sensor_2 ,voltage_2,LED_GREEN_2, LED_RED_2);


}


void validateVoltage(float input_current, float input_voltage, TcPINOUT LED_GREEN, TcPINOUT LED_RED) {
 if (input_current > current_limit) {
    // Check Voltage
    if (input_voltage < voltage_limit) {
      // LED Green on
      LED_GREEN.on();
      LED_RED.off();
    } else {
      // LED Red on
      LED_GREEN.off();
      LED_RED.on();
    }
  } else {
    // LED Off All
      LED_GREEN.off();
      LED_RED.off();
  }
}
